# Fritzing sketch Uebung_104 (saved by Fritzing 0.9.4)
breadboards: 1

parts:
  Bauteil1 = Arduino Uno (Rev3)
  R1 = Resistor [tolerance=±5% resistance=10k package=THT]
  R2 = Temperature Sensor (Thermistor) [thermistor_type=NTC package=THT]

nets:
  N1: Bauteil1.A5/SCL, R1.Pin_0, R2.pin_1
  N2: Bauteil1.GND, R2.pin_0
  N3: Bauteil1.5V, R1.Pin_1

notes:
  CS (MCP2515)
  SCK (MCP2515)
  MOSI (MCP2515)
  MISO (MCP2515)
  INT (MCP2515)
  GND (MCP2515)
  VCC (MCP2515)
  MCP2515
