# Fritzing sketch Scheduler2 (saved by Fritzing 0.9.4)
breadboards: 1

parts:
  R2 = Resistor [tolerance=±5% resistance=220 package=THT]
  Bauteil1 = Arduino Uno (Rev3)
  R4 = Resistor [tolerance=±5% resistance=220 package=THT]
  R5 = Resistor [tolerance=±5% resistance=220 package=THT]
  LED2 = LED - 5mm [color="Red (633nm)" package="5 mm [THT]"]
  LED3 = LED - 5mm [color="Orange (612nm)" package="5 mm [THT]"]
  LED4 = LED - 5mm [color="Green (565nm)" package="5 mm [THT]"]
  S1 = Pushbutton [package="[THT]"]
  R6 = Resistor [tolerance=±5% resistance=10k package=THT]

nets:
  N1: R2.Pin_0, Bauteil1.D8
  N2: R2.Pin_1, LED4.anode
  N3: Bauteil1.D10_PWM/SS, R4.Pin_0
  N4: Bauteil1.D12/MISO, R5.Pin_0
  N5: Bauteil1.GND, LED2.cathode, LED3.cathode, LED4.cathode, S1.Pin_1, S1.Pin_2
  N6: Bauteil1.D2, S1.Pin_3, S1.Pin_4, R6.Pin_1
  N7: Bauteil1.5V, R6.Pin_0
  N8: R4.Pin_1, LED3.anode
  N9: R5.Pin_1, LED2.anode
